// Digital circuit CPU.dig as structural Verilog
module CPU (
  input  Clock,
  input  [7:0] ROM,
  input  [7:0] Memory,
  output [7:0] MemAddr,
  output [7:0] MemData,
  output MemWrite,
  output [7:0] ROMAddress
);

  wire destaddr, destpc, destreg, fall, rise, setimmed, setregs;
  wire [1:0] Active_registers_q, control_1_dest, control_1_srca, control_1_srcb;
  wire [3:0] control_1_alumode;
  wire [3:2] Active_registers_q_2;
  wire [7:0] Immediate_value_q, multiplexer_1_out, multiplexer_2_out, registerfile_1_da, registerfile_1_db;

  RisingEdgeDetector risingedgedetector_1 (.In(Clock), .Out(rise));
  FallingEdgeDetector fallingedgedetector_1 (.In(Clock), .Out(fall));
  // Probe Cycle on Clock
  Control control_1 (
    .Instruction(ROM[3:0]), .Rise(rise), .SetImmed(setimmed), .SetRegs(setregs), .Dest(control_1_dest),
    .ALUMode(control_1_alumode), .SrcA(control_1_srca), .SrcB(control_1_srcb));
  Register #(.Bits(8)) Immediate_value (.D(ROM), .C(fall), .en(setimmed), .Q(Immediate_value_q));
  Register #(.Bits(4)) Active_registers (
    .D(ROM[7:4]), .C(fall), .en(setregs), .Q({Active_registers_q_2, Active_registers_q}));
  Multiplexer #(.Selector_Bits(2), .Bits(8)) multiplexer_1 (
    .sel(control_1_srcb), .in_0(Memory), .in_1(Immediate_value_q), .in_2(ROMAddress),
    .in_3(registerfile_1_db), .out(multiplexer_1_out));
  Decoder #(.Selector_Bits(2)) decoder_1 (
    .sel(control_1_dest), .out_0(destpc), .out_1(destreg), .out_2(destaddr), .out_3(MemWrite));
  Multiplexer #(.Selector_Bits(2), .Bits(8)) multiplexer_2 (
    .sel(control_1_srca), .in_0(Memory), .in_1(Immediate_value_q), .in_2(ROMAddress),
    .in_3(registerfile_1_da), .out(multiplexer_2_out));
  ALU alu_1 (
    .Mode(control_1_alumode), .A(multiplexer_2_out), .B(multiplexer_1_out), .Cin(1'b0), .Out(MemData));  // open: Cout, Zero
  Register #(.Bits(8)) Addr (.D(MemData), .C(fall), .en(destaddr), .Q(MemAddr));
  Register #(.Bits(8)) PC (.D(MemData), .C(fall), .en(destpc), .Q(ROMAddress));
  RegisterFile #(.Bits(8)) registerfile_1 (
    .Din(MemData), .we(destreg), .Rw(Active_registers_q), .C(fall), .Ra(Active_registers_q),
    .Rb(Active_registers_q_2), .Da(registerfile_1_da), .Db(registerfile_1_db));
  // Pins of 1 and 8 bits meet at MemData

  // Other names for the same wires on the sheet: destmem = MemWrite
endmodule
