// Digital circuit Control.dig as structural Verilog
module Control (
  input  [3:0] Instruction,
  input  Rise,
  output SetImmed,
  output SetRegs,
  output [1:0] Dest,
  output [3:0] ALUMode,
  output [1:0] SrcA,
  output [1:0] SrcB
);

  wire \continue ;
  wire [5:3] ControlLow_d;
  wire [7:0] Decision_d, multiplexer_1_out, uPC_q;

  Multiplexer #(.Bits(8)) multiplexer_1 (
    .sel(\continue ), .in_0({Instruction, 4'b0000}), .in_1(Decision_d), .out(multiplexer_1_out));
  Register #(.Bits(8)) uPC (.D(multiplexer_1_out), .C(Rise), .en(1'b1), .Q(uPC_q));
  // Probe uOP on uPC_q
  ROM #(.AddrBits(8), .Bits(8)) ControlLow (
    .A(uPC_q), .sel(1'b1), .D({Dest, ControlLow_d, SetRegs, SetImmed, \continue }));
  ROM #(.AddrBits(8), .Bits(8)) ControlHigh (.A(uPC_q), .sel(1'b1), .D({SrcB, SrcA, ALUMode}));
  ROM #(.AddrBits(8), .Bits(8)) Decision (.A(uPC_q), .sel(1'b1), .D(Decision_d));
  // Probe Continue uOP on \continue 

  // Notes on the sheet:
  //   contents of ControlLow (hex, n*v repeats v):
  //   1
  //   contents of ControlHigh (hex, n*v repeats v):
  //   1
  //   contents of Decision (hex, n*v repeats v):
  //   4
endmodule
